// Logisim project Binary Counter.circ as structural Verilog: 1 circuit, main circuit main
module main (
  output out_1,
  output out_2,
  output out_3,
  output out_4
);

  wire and_1_out, and_2_out, and_3_out, and_6_out, and_7_out, and_8_out, and_9_out, and_10_out, clock_1_out,
       j_k_ff_1_q, j_k_ff_1_qn, j_k_ff_2_q, j_k_ff_2_qn, j_k_ff_3_q, j_k_ff_3_qn, or_1_out, or_2_out;

  and and_1 (and_1_out, j_k_ff_1_q, j_k_ff_3_qn);
  or or_1 (or_1_out, and_1_out, j_k_ff_3_q);
  and and_2 (and_2_out, j_k_ff_3_q, j_k_ff_2_q);
  and and_3 (and_3_out, j_k_ff_2_q, j_k_ff_1_qn);
  or or_2 (or_2_out, j_k_ff_2_qn, and_3_out);
  Clock clock_1 (.out(clock_1_out));
  J_K_Flip_Flop j_k_ff_1 (
    .J(and_2_out), .clk(clock_1_out), .K(j_k_ff_2_q), .Q(j_k_ff_1_q), .Qn(j_k_ff_1_qn));  // open: preset, en, reset
  J_K_Flip_Flop j_k_ff_2 (
    .J(j_k_ff_3_q), .clk(clock_1_out), .K(or_1_out), .Q(j_k_ff_2_q), .Qn(j_k_ff_2_qn));  // open: preset, en, reset
  J_K_Flip_Flop j_k_ff_3 (
    .J(or_2_out), .clk(clock_1_out), .K(j_k_ff_3_q), .Q(j_k_ff_3_q), .Qn(j_k_ff_3_qn));  // open: preset, en, reset
  and and_4 (out_1, j_k_ff_1_q, j_k_ff_2_q, j_k_ff_3_qn);
  and and_5 (out_2, j_k_ff_1_q, j_k_ff_2_qn, j_k_ff_3_q);
  and and_6 (and_6_out, j_k_ff_1_qn, j_k_ff_2_q, j_k_ff_3_q);
  and and_7 (and_7_out, j_k_ff_1_q, j_k_ff_2_qn, j_k_ff_3_qn);
  and and_8 (and_8_out, j_k_ff_1_qn, j_k_ff_2_q, j_k_ff_3_qn);
  and and_9 (and_9_out, j_k_ff_1_q, j_k_ff_2_qn, j_k_ff_3_qn);
  and and_10 (and_10_out, j_k_ff_2_qn, j_k_ff_3_q);
  or or_3 (out_3, and_6_out, and_7_out);
  or or_4 (out_4, and_8_out, and_9_out, and_10_out);

  // Notes on the sheet:
  //   KA=B
  //   KB=AC'+C
  //   JA=BC
  //   JB=C
  //   KC=BA'+B'
  //   A
  //   B
  //   C
endmodule
