// Logisim project Segment Counter.circ as structural Verilog: 1 circuit, main circuit main
module main (
  input  in_1
);

  wire and_1_out, and_2_out, and_3_out, and_4_out, and_5_out, and_6_out, and_7_out, and_8_out, and_9_out,
       and_10_out, and_11_out, and_12_out, and_13_out, and_14_out, and_15_out, and_16_out, and_17_out,
       and_18_out, and_19_out, and_20_out, and_21_out, and_22_out, and_23_out, and_24_out, and_25_out,
       and_26_out, and_27_out, and_28_out, and_29_out, and_30_out, and_31_out, and_32_out, and_33_out,
       and_34_out, and_35_out, and_36_out, and_37_out, clock_1_out, j_k_ff_1_q, j_k_ff_1_qn, j_k_ff_2_q,
       j_k_ff_2_qn, j_k_ff_3_q, j_k_ff_3_qn, j_k_ff_4_q, j_k_ff_4_qn, or_1_out, or_2_out, or_3_out, or_4_out,
       or_5_out, or_6_out, or_7_out, or_8_out, or_9_out, or_10_out, or_11_out, or_12_out, or_13_out,
       or_14_out, or_15_out;

  and and_1 (and_1_out, j_k_ff_1_q, j_k_ff_2_qn, j_k_ff_3_qn);
  and and_2 (and_2_out, j_k_ff_1_qn, j_k_ff_2_q, j_k_ff_3_q, j_k_ff_4_q);
  and and_3 (and_3_out, j_k_ff_1_q, j_k_ff_2_qn, j_k_ff_3_qn, j_k_ff_4_q);
  and and_4 (and_4_out, j_k_ff_1_qn, j_k_ff_2_q);
  and and_5 (and_5_out, j_k_ff_1_qn, j_k_ff_2_qn, j_k_ff_3_q, j_k_ff_4_q);
  and and_6 (and_6_out, j_k_ff_1_q, j_k_ff_2_qn, j_k_ff_3_qn);
  and and_7 (and_7_out, j_k_ff_1_qn, j_k_ff_2_qn);
  and and_8 (and_8_out, j_k_ff_1_qn, j_k_ff_2_q, j_k_ff_3_q, j_k_ff_4_q);
  and and_9 (and_9_out, j_k_ff_1_qn, j_k_ff_3_q);
  and and_10 (and_10_out, j_k_ff_1_qn, j_k_ff_3_qn, j_k_ff_4_q);
  and and_11 (and_11_out, j_k_ff_1_qn, j_k_ff_3_qn);
  and and_12 (and_12_out, j_k_ff_1_q, j_k_ff_2_qn, j_k_ff_3_qn);
  and and_13 (and_13_out, j_k_ff_1_qn, j_k_ff_3_q, j_k_ff_4_q);
  or or_1 (or_1_out, j_k_ff_4_q, j_k_ff_4_qn);
  or or_2 (or_2_out, j_k_ff_4_q, j_k_ff_4_qn);
  or or_3 (or_3_out, and_1_out, and_2_out);
  or or_4 (or_4_out, j_k_ff_1_qn, and_3_out);
  or or_5 (or_5_out, and_4_out, and_5_out);
  or or_6 (or_6_out, and_6_out, and_7_out, and_8_out);
  or or_7 (or_7_out, and_9_out, and_10_out);
  or or_8 (or_8_out, and_11_out, and_12_out, and_13_out);
  J_K_Flip_Flop j_k_ff_1 (
    .J(or_3_out), .clk(clock_1_out), .K(or_4_out), .Q(j_k_ff_1_q), .Qn(j_k_ff_1_qn));  // open: preset, en, reset
  J_K_Flip_Flop j_k_ff_2 (
    .J(or_5_out), .clk(clock_1_out), .K(or_6_out), .Q(j_k_ff_2_q), .Qn(j_k_ff_2_qn));  // open: preset, en, reset
  J_K_Flip_Flop j_k_ff_3 (
    .J(or_7_out), .clk(clock_1_out), .K(or_8_out), .Q(j_k_ff_3_q), .Qn(j_k_ff_3_qn));  // open: preset, en, reset
  J_K_Flip_Flop j_k_ff_4 (
    .J(or_1_out), .clk(clock_1_out), .K(or_2_out), .Q(j_k_ff_4_q), .Qn(j_k_ff_4_qn));  // open: preset, en, reset
  and and_14 (and_14_out, j_k_ff_1_q, j_k_ff_2_qn, j_k_ff_3_qn);
  and and_15 (and_15_out, j_k_ff_1_qn, j_k_ff_2_q, j_k_ff_3_qn);
  and and_16 (and_16_out, j_k_ff_1_qn, j_k_ff_2_qn, j_k_ff_3_q);
  and and_17 (and_17_out, j_k_ff_1_qn, j_k_ff_2_q, j_k_ff_2_q, j_k_ff_4_qn);
  and and_18 (and_18_out, j_k_ff_1_qn, j_k_ff_2_q);
  and and_19 (and_19_out, j_k_ff_1_q, j_k_ff_2_qn, j_k_ff_3_qn);
  and and_20 (and_20_out, j_k_ff_1_qn, j_k_ff_3_q);
  and and_21 (and_21_out, j_k_ff_1_q, j_k_ff_2_qn, j_k_ff_3_qn);
  and and_22 (and_22_out, j_k_ff_1_qn, j_k_ff_2_q, j_k_ff_3_qn, j_k_ff_4_q);
  and and_23 (and_23_out, j_k_ff_1_q, j_k_ff_2_qn, j_k_ff_3_qn);
  and and_24 (and_24_out, j_k_ff_1_qn, j_k_ff_2_qn, j_k_ff_3_q);
  and and_25 (and_25_out, j_k_ff_1_qn, j_k_ff_2_q, j_k_ff_3_q, j_k_ff_4_q);
  and and_26 (and_26_out, j_k_ff_1_qn, j_k_ff_2_q, j_k_ff_3_qn, j_k_ff_4_qn);
  and and_27 (and_27_out, j_k_ff_1_qn, j_k_ff_2_qn, j_k_ff_3_qn, j_k_ff_4_q);
  and and_28 (and_28_out, j_k_ff_1_qn, j_k_ff_3_q, j_k_ff_4_qn);
  and and_29 (and_29_out, j_k_ff_1_q, j_k_ff_2_qn, j_k_ff_3_qn, j_k_ff_4_qn);
  and and_30 (and_30_out, j_k_ff_1_q, j_k_ff_2_qn, j_k_ff_3_qn);
  and and_31 (and_31_out, j_k_ff_1_qn, j_k_ff_2_qn, j_k_ff_3_q);
  and and_32 (and_32_out, j_k_ff_1_qn, j_k_ff_2_q, j_k_ff_3_qn, j_k_ff_4_q);
  and and_33 (and_33_out, j_k_ff_1_qn, j_k_ff_2_q, j_k_ff_3_q, j_k_ff_4_qn);
  and and_34 (and_34_out, j_k_ff_1_q, j_k_ff_2_qn, j_k_ff_3_qn);
  and and_35 (and_35_out, j_k_ff_1_qn, j_k_ff_2_q, j_k_ff_3_qn);
  and and_36 (and_36_out, j_k_ff_1_qn, j_k_ff_2_qn, j_k_ff_4_q);
  and and_37 (and_37_out, j_k_ff_1_qn, j_k_ff_2_q, j_k_ff_3_q, j_k_ff_4_qn);
  or or_9 (or_9_out, and_14_out, and_15_out, and_16_out, and_17_out);
  or or_10 (or_10_out, and_18_out, and_19_out);
  or or_11 (or_11_out, and_20_out, and_21_out, and_22_out);
  or or_12 (or_12_out, and_23_out, and_24_out, and_25_out, and_26_out, and_27_out);
  or or_13 (or_13_out, and_28_out, and_29_out);
  or or_14 (or_14_out, and_30_out, and_31_out, and_32_out, and_33_out);
  or or_15 (or_15_out, and_34_out, and_35_out, and_36_out, and_37_out);
  _7_Segment_Display u_7_segment_display_1 (
    .g(or_9_out), .f(or_10_out), .a(or_11_out), .b(or_12_out), .e(or_13_out), .d(or_14_out), .c(or_15_out),
    .dp(in_1));
  Clock clock_1 (.out(clock_1_out));

  // Notes on the sheet:
  //   D
  //   A
  //   B
  //   C
  //   T
  //   U
  //   V
  //   W
  //   X
  //   Y
  //   Z
endmodule
