// Logisim project counter.circ as structural Verilog: 1 circuit, main circuit main
module main (
  input  F
);

  wire and_1_out, and_2_out, and_3_out, and_4_out, and_5_out, and_6_out, and_7_out, and_8_out, and_9_out,
       and_10_out, clock_1_out, d_ff_1_q, d_ff_1_qn, d_ff_2_q, d_ff_2_qn, d_ff_3_q, d_ff_3_qn, not_1_out,
       or_1_out, or_2_out, or_3_out;

  not not_1 (not_1_out, F);
  and and_1 (and_1_out, d_ff_1_qn, d_ff_2_q, d_ff_3_q, not_1_out);
  and and_2 (and_2_out, d_ff_1_q, d_ff_2_qn, d_ff_3_qn);
  and and_3 (and_3_out, d_ff_1_q, d_ff_2_qn, d_ff_3_q, F);
  and and_4 (and_4_out, d_ff_1_qn, d_ff_2_q, d_ff_3_qn);
  and and_5 (and_5_out, d_ff_1_qn, d_ff_2_q, d_ff_3_q, F);
  and and_6 (and_6_out, d_ff_1_qn, d_ff_2_qn, d_ff_3_q, not_1_out);
  and and_7 (and_7_out, d_ff_1_qn, d_ff_3_qn, not_1_out, not_1_out);
  and and_8 (and_8_out, d_ff_1_qn, d_ff_3_q, F);
  and and_9 (and_9_out, d_ff_1_q, d_ff_2_qn, d_ff_3_qn, not_1_out);
  and and_10 (and_10_out, d_ff_1_q, d_ff_2_qn, d_ff_3_q, F);
  or or_1 (or_1_out, and_1_out, and_2_out, and_3_out);
  or or_2 (or_2_out, and_4_out, and_5_out, and_6_out);
  or or_3 (or_3_out, and_7_out, and_8_out, and_9_out, and_10_out);
  Clock clock_1 (.out(clock_1_out));
  D_Flip_Flop d_ff_1 (.clk(clock_1_out), .D(or_1_out), .Q(d_ff_1_q), .Qn(d_ff_1_qn));  // open: preset, en, reset
  D_Flip_Flop d_ff_2 (.clk(clock_1_out), .D(or_2_out), .Q(d_ff_2_q), .Qn(d_ff_2_qn));  // open: preset, en, reset
  D_Flip_Flop d_ff_3 (.clk(clock_1_out), .D(or_3_out), .Q(d_ff_3_q), .Qn(d_ff_3_qn));  // open: preset, en, reset

  // Notes on the sheet:
  //   A
  //   B
  //   C
endmodule
